# Fritzing sketch FDL3 (saved by Fritzing 0.9.4)

parts:
  920KV_Motor1 = DJI 920 KV Motor
  DJI_ESC_30A2 = DJI 30A ESC
  920KV_Motor2 = DJI 920 KV Motor
  Digispark1 = Digispark
  DJI_ESC_30A3 = DJI 30A ESC
  BAT1 = Battery Holders [package=lipo-1100mAh]
  Digital_Panel_Meter_Voltage_DMS-20PC_by_Murata1 = Digital Panel Meter, Voltage, DMS-20PC  # not connected
  S1 = SWITCH-SPST-2 [package=switch-spst-vertical]
  S3 = SWITCH-MOMENTARY-2 [package=tactile-pth-12mm]
  R1 = Resistor [tolerance=±5% resistance=220 package="2512 [SMD]"]

nets:
  N1: 920KV_Motor1.w, DJI_ESC_30A2.W
  N2: 920KV_Motor1.v, DJI_ESC_30A2.V
  N3: 920KV_Motor1.u, DJI_ESC_30A2.U
  N4: DJI_ESC_30A2.GROUND, BAT1.-
  N5: DJI_ESC_30A2.+12V, S1.P
  N6: DJI_ESC_30A2.DATA_OUT, Digispark1.P2
  N7: 920KV_Motor2.w, DJI_ESC_30A3.W
  N8: 920KV_Motor2.v, DJI_ESC_30A3.V
  N9: 920KV_Motor2.u, DJI_ESC_30A3.U
  N10: Digispark1.VCC, S3.1
  N11: Digispark1.P4, S3.2, R1.Pin_1
  N12: BAT1.+, S1.O

custom parts:
  DJI 920 KV Motor: DJI Brushless Outrunner 2212/920K Motor F330-550
  Digispark: The Digispark is an Attiny85 based microcontroller development board similar to the Arduino line, only cheaper, smaller, and a bit less powerful. With a whole host of shields to extend its functionality and the ability to use the familiar Arduino IDE the Digispark is a great way to jump into electronics, or perfect for when an Arduino is too big or too much.
